# Fritzing sketch CS_AIMBOT_v2 (saved by Fritzing 0.9.3b)
breadboards: 4

parts:
  U1 = ESP32-38PinWide [part_number=ESP32-38PinWide]
  A1 = DM860A Stepper Motor Driver
  VCC1 = Battery
  U2 = LM2596 step down module
  VCC4 = Battery
  U3 = LM2596 step down module
  VCC5 = Battery
  A4 = TXS0108E module
  RE1 = KY-040 Rotary encoder [package=THT]
  RE2 = KY-040 Rotary encoder [package=THT]
  J1 = Basic Servo
  L1 = Solenoid
  M1 = Stepper Motor - Bipolar
  M2 = Stepper Motor - Bipolar
  M3 = Stepper Motor - Bipolar
  A5 = TXS0108E module
  Q1 = Basic FET N-Channel [package="TO220 [THT]"]
  D1 = Rectifier Diode [part_number=1N4007 package="300 mil [THT]"]
  R1 = Resistor [tolerance=±5% resistance=10k package="0805 [SMD]"]
  R2 = Resistor [tolerance=±5% resistance=220 package="2512 [SMD]"]
  A3 = DM860A Stepper Motor Driver
  A2 = DM860A Stepper Motor Driver

nets:
  N1: U1.3.3, A4.Pin_20, A5.Pin_20
  N2: U1.GPIO34, A4.Pin_12
  N3: U1.GPIO35, A4.Pin_13
  N4: U1.GPIO32, A4.Pin_14
  N5: U1.GPIO33, A4.Pin_15
  N6: U1.GPIO25, A4.Pin_19
  N7: U1.GPIO26, A4.Pin_18
  N8: U1.GPIO27, A4.Pin_17
  N9: U1.GPIO14, A4.Pin_16
  GND: U1.GND, U3.IN-, U3.OUT-, VCC5.-, J1.gnd, Q1.source, R1.Pin_1
  GND_2: U1.GPIO11, U2.IN-, U2.OUT-, VCC4.-, RE1.GND, RE2.GND
  VCC: U1.VIN, U2.OUT+, A4.Pin_1, RE1.Vcc, RE2.Vcc, A5.Pin_1
  N10: U1.GPIO4, R2.Pin_0
  N11: U1.GPIO18, A5.Pin_18
  N12: U1.GPIO19, A5.Pin_19
  N13: U1.GPIO21, J1.pulse
  N14: A1.B-, M1.D
  N15: A1.B+, M1.B
  N16: A1.A-, M1.C
  N17: A1.A+, M1.A
  N18: A1.VDC, VCC1.+, A3.VDC, A2.VDC
  GND_3: A1.GND, VCC1.-, A3.GND, A2.GND
  N19: A1.DIR+(+5V), A4.Pin_3
  N20: A1.PUL+(+5V), A4.Pin_2
  N21: U2.IN+, VCC4.+
  N22: U3.IN+, VCC5.+
  N23: U3.OUT+, J1.vcc, L1.pin2, D1.cathode
  N24: A4.Pin_4, A2.PUL+(+5V)
  N25: A4.Pin_5, A2.DIR+(+5V)
  N26: A4.Pin_6, RE2.CLK
  N27: A4.Pin_7, RE2.DT
  N28: A4.Pin_8, RE1.CLK
  N29: A4.Pin_9, RE1.DT
  N30: L1.pin1, Q1.drain, D1.anode
  N31: M2.A, A2.A+
  N32: M2.C, A2.A-
  N33: M2.B, A2.B+
  N34: M2.D, A2.B-
  N35: M3.A, A3.A+
  N36: M3.C, A3.A-
  N37: M3.B, A3.B+
  N38: A5.Pin_2, A3.PUL+(+5V)
  N39: A5.Pin_3, A3.DIR+(+5V)
  N40: Q1.gate, R1.Pin_0, R2.Pin_1

notes:
  36V plus zaslacz
  36v+
  36 - 5 V
  36 - 6 V
  NEMA 23 - dwu wałowe do tylniego nakładamy enkoder
  NEMA 17
  zakładam, że:
  CLK to faza A enkodera,
  DT to sygnał B,
  enkodera
  Na razie pomijamy fazę C

custom parts:
  ESP32-38PinWide: Generic 38-Pin ESP32 with wide format (only access to one side of pins on a breadboard) based on Stephen Lilley's HiLetgo ESP-WROOM-32 ESP32 ESP-32S Development Board.
  DM860A Stepper Motor Driver: DM860A is a type of two-phase hybrid stepping motor driver, The drive voltage of which is from 24VDC to 80VDC. It is designed for use with 2-phase hybrid stepper motor of all kinds with 57mm to 110mm outside diameter and less than 8.0A phase current. Mar 2023: Correct pcb layerId as the part won't save correctly in a .fzz file as is.
  LM2596 step down module: LM2596 DC-DC step down power supply module 3 A.
  TXS0108E module: TXS0108E Logic Level Shifter Bi-Directional Module 3.3V 5V 8 Channel Logic Level Switching Shifter High Speed.
  KY-040 Rotary encoder: KY-040 Rotary Encoder with switch on breakout borad from AZ Delivery
