# Fritzing sketch ELECTRONIC_SCHEME_FINAL_VERSION (saved by Fritzing 0.9.3b)
breadboards: 1

parts:
  A1 = DM860A Stepper Motor Driver
  A3 = DM860A Stepper Motor Driver
  A2 = DM860A Stepper Motor Driver
  VCC1 = Battery
  M1 = Stepper Motor - Bipolar
  M2 = Stepper Motor - Bipolar
  M3 = Stepper Motor - Bipolar
  U1 = LM2596 step down module
  VCC2 = Battery  # not connected
  U2 = ESP32-38PinWide [part_number=ESP32-38PinWide]
  J1 = Basic Servo
  U3 = ENCODER_2LED [package=encoder_led_2]
  U4 = ENCODER_2LED [package=encoder_led_2]
  R1 = Resistor [tolerance=±5% resistance=4.7k package="1206 [SMD]"]
  R2 = Resistor [tolerance=±5% resistance=4.7k package="1206 [SMD]"]
  R3 = Resistor [tolerance=±5% resistance=4.7k package="1206 [SMD]"]
  R4 = Resistor [tolerance=±5% resistance=4.7k package="1206 [SMD]"]
  A4 = 2 channel relay module [package=THT]
  L1 = Solenoid
  L2 = Solenoid
  D1 = Rectifier Diode [part_number=1N4001 package="300 mil [THT]"]
  D2 = Rectifier Diode [part_number=1N4001 package="300 mil [THT]"]
  U5 = LM2596 step down module
  VCC3 = Battery  # not connected
  JL012-13-5_1 = JL012-13-5.2 Lever (Limit) Switch SPDT + NO + NC [part_number=JL012-13-5.2]
  JL012-13-5_2 = JL012-13-5.2 Lever (Limit) Switch SPDT + NO + NC [part_number=JL012-13-5.2]
  JL012-13-5_3 = JL012-13-5.2 Lever (Limit) Switch SPDT + NO + NC [part_number=JL012-13-5.2]

nets:
  N1: A1.B-, M1.D
  N2: A1.B+, M1.B
  N3: A1.A-, M1.C
  N4: A1.A+, M1.A
  N5: A1.VDC, A2.VDC, VCC1.+
  GND: A1.GND, A2.GND, VCC1.-
  GND_2: A1.DIR-(DIR), A3.DIR-(DIR), A2.DIR-(DIR), U1.IN-, U1.OUT-, U2.GND, J1.gnd, U4.C, A4.pin_14, L1.pin1, L2.pin1, D1.anode, D2.anode, U5.IN-, U5.OUT-, JL012-13-5_1.C
  N6: A1.DIR+(+5V), U2.GPIO22
  N7: A1.PUL+(+5V), U2.GPIO23
  N8: A3.B-, M3.D
  N9: A3.B+, M3.B
  N10: A3.A-, M3.C
  N11: A3.A+, M3.A
  N12: A3.DIR+(+5V), U2.GPIO17
  N13: A3.PUL+(+5V), U2.GPIO12
  N14: A2.B-, M2.D
  N15: A2.B+, M2.B
  N16: A2.A-, M2.C
  N17: A2.A+, M2.A
  N18: A2.DIR+(+5V), U2.GPIO19
  N19: A2.PUL+(+5V), U2.GPIO21
  VIN: U1.OUT+, U2.VIN, J1.vcc, U4.B, A4.pin_13
  N20: U2.3.3, R1.Pin_0, R2.Pin_0, R3.Pin_0, R4.Pin_0
  N21: U2.GPIO32, U3.-, R2.Pin_1
  N22: U2.GPIO33, U3.SW, R1.Pin_1
  N23: U2.GPIO25, J1.pulse
  N24: U2.GPIO26, A4.pin_15
  N25: U2.GPIO27, A4.pin_16
  N26: U2.GPIO14, JL012-13-5_3.NC
  N27: U2.GPIO13, JL012-13-5_2.NC
  N28: U2.GPIO16, JL012-13-5_1.NC
  N29: U2.GPIO5, U4.SW, R3.Pin_1
  N30: U2.GPIO18, U4.-, R4.Pin_1
  N31: A4.pin_1, L1.pin2, D1.cathode
  N32: A4.pin_2, U5.OUT+
  N33: A4.pin_4, L2.pin2, D2.cathode

notes:
  36 V
  NEMA 23
  NEMA17
  STEP DOWN 36V TO 5V
  STEP DOWN 36V TO 12V
  LIMIT SWITCH
  X
  LIMIT SWITCH
  Y
  LIMIT SWITCH
  Z

custom parts:
  DM860A Stepper Motor Driver: DM860A is a type of two-phase hybrid stepping motor driver, The drive voltage of which is from 24VDC to 80VDC. It is designed for use with 2-phase hybrid stepper motor of all kinds with 57mm to 110mm outside diameter and less than 8.0A phase current. Mar 2023: Correct pcb layerId as the part won't save correctly in a .fzz file as is.
  LM2596 step down module: LM2596 DC-DC step down power supply module 3 A.
  ESP32-38PinWide: Generic 38-Pin ESP32 with wide format (only access to one side of pins on a breadboard) based on Stephen Lilley's HiLetgo ESP-WROOM-32 ESP32 ESP-32S Development Board.
  2 channel relay module: 2 channel Relay Module 5V 12V 24V High and Low Level Trigger Relay Control With Optocoupler Two Way relays DC 5 V 12 V 24 V Volt.
  JL012-13-5.2 Lever (Limit) Switch SPDT + NO + NC: Micro Switch; Model No.: JL012-13.5-2; Actuator Action: Momentary; Actuator Type: Hinge Lever; Contact Configuration: 1NO, 1NC (SPDT) Temperature -25~65℃；Relative humidity: below 85%; Rate Voltage: 125V AC; Rated Current: 1A.
